// Logisim project CPU01.circ as structural Verilog: 9 circuits, main circuit main
module flip_flop_alterado (
  input  JMP,
  input  END,
  input  CLK,
  input  Entrada,
  input  CLR,
  output Q,
  output Q_prime
);

  wire and_1_out, and_2_out, or_1_out;

  and and_1 (and_1_out, ~END, JMP);  // AND_Gate
  and and_2 (and_2_out, END, JMP);
  T_Flip_Flop #(.trigger("falling")) t_ff_1 (
    .clk(CLK), .T(Entrada), .Q(Q), .Qn(Q_prime), .preset(and_2_out), .reset(or_1_out));
  or or_1 (or_1_out, and_1_out, CLR);
endmodule

module Count8 (
  input  [3:0] Endereco,
  input  CLK,
  input  JUMP,
  input  CLR,
  input  Master_CLR,
  output [7:0] \Saída 
);

  wire and_1_out, and_2_out, and_3_out, and_4_out, and_5_out, and_6_out, and_7_out, or_1_out;

  and and_1 (and_1_out, ~CLK, JUMP);  // AND_Gate
  flip_flop_alterado flip_flop_alterado_1 (
    .CLK(CLK), .Entrada(1'b1), .Q(\Saída [0]), .JMP(and_1_out), .END(Endereco[0]), .CLR(or_1_out));  // open: Q_prime
  flip_flop_alterado flip_flop_alterado_2 (
    .CLK(CLK), .Entrada(\Saída [0]), .Q(\Saída [1]), .JMP(and_1_out), .END(Endereco[1]), .CLR(or_1_out));  // open: Q_prime
  and and_2 (and_2_out, \Saída [1], \Saída [0]);
  flip_flop_alterado flip_flop_alterado_3 (
    .CLK(CLK), .Entrada(and_2_out), .Q(\Saída [2]), .JMP(and_1_out), .END(Endereco[2]), .CLR(or_1_out));  // open: Q_prime
  and and_3 (and_3_out, \Saída [2], and_2_out);
  Hex_Digit_Display hex_digit_display_1 (.value(\Saída [7:4]));  // open: dp
  flip_flop_alterado flip_flop_alterado_4 (
    .CLK(CLK), .Entrada(and_3_out), .Q(\Saída [3]), .JMP(and_1_out), .END(Endereco[3]), .CLR(or_1_out));  // open: Q_prime
  and and_4 (and_4_out, \Saída [3], and_3_out);
  Hex_Digit_Display hex_digit_display_2 (.value(\Saída [3:0]));  // open: dp
  flip_flop_alterado flip_flop_alterado_5 (
    .CLK(CLK), .Entrada(and_4_out), .Q(\Saída [4]), .JMP(and_1_out), .END(1'b0), .CLR(or_1_out));  // open: Q_prime
  or or_1 (or_1_out, CLR, Master_CLR);
  and and_5 (and_5_out, \Saída [4], and_4_out);
  flip_flop_alterado flip_flop_alterado_6 (
    .CLK(CLK), .Entrada(and_5_out), .Q(\Saída [5]), .JMP(and_1_out), .END(1'b0), .CLR(or_1_out));  // open: Q_prime
  and and_6 (and_6_out, \Saída [5], and_5_out);
  flip_flop_alterado flip_flop_alterado_7 (
    .CLK(CLK), .Entrada(and_6_out), .Q(\Saída [6]), .JMP(and_1_out), .END(1'b0), .CLR(or_1_out));  // open: Q_prime
  and and_7 (and_7_out, \Saída [6], and_6_out);
  flip_flop_alterado flip_flop_alterado_8 (
    .CLK(CLK), .Entrada(and_7_out), .Q(\Saída [7]), .JMP(and_1_out), .END(1'b0), .CLR(or_1_out));  // open: Q_prime

  // Other names for the same wires on the sheet: E0 = Endereco[0]; E1 = Endereco[1]; E2 = Endereco[2];
  //   E3 = Endereco[3]
endmodule

module main (
  output [3:0] out_1,
  output [15:0] out_2
);

  wire CLEAR_ROM, CLR_REG, JUMP, K0, K1, K2, K3, L0, L1, L2, L3, L4, L5, L6, L7, L8, L9, LOAD1, LOAD2, S0,
       S1, S2, S3, S4, S5, S6, S7, S8, S9;
  wire [1:0] ULA_Selector;
  wire [3:0] Destiny, HEX0, HEX1, Origin;

  Hex_Digit_Display hex_digit_display_1 (.value(out_2[15:12]));  // open: dp
  LED u_L9 (.in(L9));
  LED u_L8 (.in(L8));
  // DipSwitch #(.NSwitches(1)) S8: pin names not known; wires that end beside it: S8
  // DipSwitch #(.NSwitches(1)) S9: pin names not known; wires that end beside it: S9
  Hex_Digit_Display hex_digit_display_2 (.value(out_2[7:4]));  // open: dp
  Hex_Digit_Display hex_digit_display_3 (.value(out_2[11:8]));  // open: dp
  LED u_L7 (.in(L7));
  LED u_L6 (.in(L6));
  LED u_L5 (.in(L5));
  // DipSwitch #(.NSwitches(1)) S6: pin names not known; wires that end beside it: S6
  // DipSwitch #(.NSwitches(1)) S5: pin names not known; wires that end beside it: S5
  // DipSwitch #(.NSwitches(1)) S7: pin names not known; wires that end beside it: S7
  UC UC (
    .Dados(out_2), .REG1(HEX1), .REG2(HEX0), .LOAD1(LOAD1), .LOAD2(LOAD2), .ULA_Selector(ULA_Selector),
    .CLR_ROM(CLEAR_ROM), .JUMP(JUMP), .Operando(out_1), .CLR_REG(CLR_REG), .Origin(Origin));
  Hex_Digit_Display hex_digit_display_4 (.value(out_2[3:0]));  // open: dp
  LED u_L3 (.in(L3));
  LED u_L4 (.in(L4));
  // DipSwitch #(.NSwitches(1)) S4: pin names not known; wires that end beside it: S4
  // DipSwitch #(.NSwitches(1)) S3: pin names not known; wires that end beside it: S3
  // DipSwitch #(.NSwitches(1)) S2: pin names not known; wires that end beside it: S2
  Count8 Count8 (
    .Endereco(out_1), .CLK(S9), .JUMP(JUMP), .\Saída ({L7, L6, L5, L4, L3, L2, L1, L0}), .Master_CLR(S0),
    .CLR(CLEAR_ROM));
  Hex_Digit_Display hex_digit_display_5 (.value(HEX1));  // open: dp
  LED u_L0 (.in(L0));
  LED u_L1 (.in(L1));
  LED u_L2 (.in(L2));
  // DipSwitch #(.NSwitches(1)) S1: pin names not known; wires that end beside it: S1
  // DipSwitch #(.NSwitches(1)) S0: pin names not known; wires that end beside it: S0
  Hex_Digit_Display hex_digit_display_6 (.value(HEX0));  // open: dp
  Button u_K2 (.out(K2));
  Button u_K3 (.out(K3));
  ROM_256x16 ROM_256x16 (.in_1({L7, L6, L5, L4, L3, L2, L1, L0}), .out_4(out_2), .in_2(S9), .in_3(S0));
  Button u_K1 (.out(K1));
  Button u_K0 (.out(K0));
  // Digital_Oscilloscope #(.nState(16)) digital_oscilloscope_1: pin names not known; wires that end beside it: S9, L0, L1, L2, L3, L4, L5, L6, L7
  Reg4 Reg4 (.Clock(S9), .Clear_Reg(CLR_REG), .Clear_Master(S0), .LOAD(LOAD1), .REG_OUT(HEX1), .Data_In(Destiny));
  ULA4 ULA4 (.ULA(ULA_Selector), .Operando(out_1), .Origin(Origin), .Destiny(Destiny));
  Reg4 Reg4_2 (.Clock(S9), .Clear_Reg(CLR_REG), .Clear_Master(S0), .LOAD(LOAD2), .REG_OUT(HEX0), .Data_In(Destiny));

  // Other names for the same wires on the sheet: DADOS[15:0] = out_2; HEX2[3:0] = out_2[3:0]; HEX3[3:0] = out_2[7:4];
  //   HEX4[3:0] = out_2[11:8]; HEX5[3:0] = out_2[15:12]; Operando[3:0] = out_1; REG1[3:0] = HEX1; REG2[3:0] = HEX0
endmodule

module divisorBits (
  input  [15:0] in_1,
  output [3:0] Operando,
  output [3:0] \Disponível ,
  output [1:0] ULA,
  output [1:0] JUMP,
  output [1:0] RgTO,
  output [1:0] RgIn
);


  assign \Disponível  = in_1[7:4];
  assign JUMP = in_1[11:10];
  assign Operando = in_1[3:0];
  assign RgIn = in_1[13:12];
  assign RgTO = in_1[15:14];
  assign ULA = in_1[9:8];
endmodule

module ROM_256x16 (
  input  [7:0] in_1,
  input  in_2,
  input  in_3,
  output [15:0] out_4
);

  wire [15:0] rom_1_data;

  ROM #(.dataWidth(16), .Select("low")) rom_1 (.addr(in_1), .data(rom_1_data));
  Register #(.width(16), .Select("low")) register_1 (.D(rom_1_data), .Q(out_4), .clk(in_2), .clr(in_3));  // open: en

  // Notes on the sheet:
  //   contents of rom_1 (hex, n*v repeats v):
  //   6004 9102 6201 6305 9002 6002 9003 400 c0d 4*0 9002 6302 6101 9302 6200 6003 800
endmodule

module Jump_Control (
  input  [1:0] in_1,
  output ULA_LOAD,
  output CLEAR_REG,
  output CLEAR_ROM,
  output JUMP
);

  and and_1 (ULA_LOAD, ~in_1[0], ~in_1[1]);  // AND_Gate
  and and_2 (CLEAR_REG, in_1[0], ~in_1[1]);  // AND_Gate
  and and_3 (CLEAR_ROM, ~in_1[0], in_1[1]);  // AND_Gate
  and and_4 (JUMP, in_1[0], in_1[1]);
endmodule

module ULA4 (
  input  [1:0] ULA,
  input  [3:0] Operando,
  input  [3:0] Origin,
  output [3:0] Destiny
);

  wire Operando_2, Operando_x_2, RG_In___Operando, RG_In_Operando;
  wire [3:0] adder_1_out, and_5_out, and_9_out, and_13_out, and_17_out, divider_1_out, multiplier_1_out,
       subtractor_1_out;

  and and_1 (RG_In_Operando, ~ULA[0], ~ULA[1]);  // AND_Gate
  and and_2 (Operando_x_2, ULA[0], ~ULA[1]);  // AND_Gate
  and and_3 (RG_In___Operando, ~ULA[0], ULA[1]);  // AND_Gate
  and and_4 (Operando_2, ULA[0], ULA[1]);
  Adder #(.width(4)) adder_1 (.a(Operando), .b(Origin), .out(adder_1_out));  // open: cin, cout
  Multiplier #(.width(4)) multiplier_1 (.a(Operando), .b(4'b0010), .out(multiplier_1_out));  // open: cin, cout
  Subtractor #(.width(4)) subtractor_1 (.a(Origin), .b(Operando), .out(subtractor_1_out));  // open: bin, bout
  Divider #(.width(4)) divider_1 (.a(Operando), .b(4'b0010), .out(divider_1_out));  // open: upper, rem
  and and_5 (and_5_out[0], adder_1_out[0], RG_In_Operando);
  and and_6 (and_5_out[1], adder_1_out[1], RG_In_Operando);
  and and_7 (and_5_out[2], adder_1_out[2], RG_In_Operando);
  and and_8 (and_5_out[3], adder_1_out[3], RG_In_Operando);
  and and_9 (and_9_out[0], multiplier_1_out[0], Operando_x_2);
  and and_10 (and_9_out[1], multiplier_1_out[1], Operando_x_2);
  and and_11 (and_9_out[2], multiplier_1_out[2], Operando_x_2);
  and and_12 (and_9_out[3], multiplier_1_out[3], Operando_x_2);
  and and_13 (and_13_out[0], subtractor_1_out[0], RG_In___Operando);
  and and_14 (and_13_out[1], subtractor_1_out[1], RG_In___Operando);
  and and_15 (and_13_out[2], subtractor_1_out[2], RG_In___Operando);
  and and_16 (and_13_out[3], subtractor_1_out[3], RG_In___Operando);
  and and_17 (and_17_out[0], divider_1_out[0], Operando_2);
  and and_18 (and_17_out[1], divider_1_out[1], Operando_2);
  and and_19 (and_17_out[2], divider_1_out[2], Operando_2);
  and and_20 (and_17_out[3], divider_1_out[3], Operando_2);
  Multiplexer #(.select(2), .width(4), .enable("false")) multiplexer_1 (
    .in0(and_5_out), .in1(and_9_out), .in2(and_13_out), .in3(and_17_out), .out(Destiny), .sel(ULA));

  // Other names for the same wires on the sheet: Operacao[1:0] = ULA
endmodule

module Reg4 (
  input  Clock,
  input  Clear_Reg,
  input  Clear_Master,
  input  LOAD,
  input  [3:0] Data_In,
  output [3:0] REG_OUT
);

  wire multiplexer_1_out, multiplexer_2_out, multiplexer_3_out, multiplexer_4_out, or_1_out;

  or or_1 (or_1_out, Clear_Reg, Clear_Master);
  D_Flip_Flop #(.trigger("falling")) d_ff_1 (
    .clk(Clock), .D(multiplexer_1_out), .Q(REG_OUT[3]), .reset(or_1_out));  // open: Qn, preset
  Multiplexer #(.enable("false")) multiplexer_1 (
    .in0(REG_OUT[3]), .in1(Data_In[3]), .out(multiplexer_1_out), .sel(LOAD));
  D_Flip_Flop #(.trigger("falling")) d_ff_2 (
    .clk(Clock), .D(multiplexer_2_out), .Q(REG_OUT[2]), .reset(or_1_out));  // open: Qn, preset
  Multiplexer #(.enable("false")) multiplexer_2 (
    .in0(REG_OUT[2]), .in1(Data_In[2]), .out(multiplexer_2_out), .sel(LOAD));
  Multiplexer #(.enable("false")) multiplexer_3 (
    .in0(REG_OUT[1]), .in1(Data_In[1]), .out(multiplexer_3_out), .sel(LOAD));
  D_Flip_Flop #(.trigger("falling")) d_ff_3 (
    .clk(Clock), .D(multiplexer_3_out), .Q(REG_OUT[1]), .reset(or_1_out));  // open: Qn, preset
  Multiplexer #(.enable("false")) multiplexer_4 (
    .in0(REG_OUT[0]), .in1(Data_In[0]), .out(multiplexer_4_out), .sel(LOAD));
  D_Flip_Flop #(.trigger("falling")) d_ff_4 (
    .clk(Clock), .D(multiplexer_4_out), .Q(REG_OUT[0]), .reset(or_1_out));  // open: Qn, preset
endmodule

module UC (
  input  [15:0] Dados,
  input  [3:0] REG1,
  input  [3:0] REG2,
  output LOAD1,
  output LOAD2,
  output [3:0] Operando,
  output [1:0] ULA_Selector,
  output CLR_REG,
  output CLR_ROM,
  output [3:0] Origin,
  output JUMP
);

  wire LOAD;
  wire [1:0] divisorbits_1_jump, REG_IN, REG_TO;

  Demultiplexer #(.select(2), .enable("false")) demultiplexer_1 (
    .out1(LOAD1), .out2(LOAD2), .in(LOAD), .sel(REG_TO));  // open: out0, out3
  Multiplexer #(.select(2), .width(4), .enable("false")) multiplexer_1 (
    .in1(REG1), .in2(REG2), .out(Origin), .sel(REG_IN));  // open: in0, in3
  divisorBits divisorbits_1 (
    .in_1(Dados), .ULA(ULA_Selector), .JUMP(divisorbits_1_jump), .Operando(Operando), .RgTO(REG_TO),
    .RgIn(REG_IN));  // open: Disponível
  Jump_Control jump_control_1 (
    .in_1(divisorbits_1_jump), .ULA_LOAD(LOAD), .CLEAR_REG(CLR_REG), .CLEAR_ROM(CLR_ROM), .JUMP(JUMP));
endmodule
