// Logisim project Contador8bits.circ as structural Verilog: 2 circuits, main circuit flip-flop alterado
module flip_flop_alterado (
  input  JMP,
  input  END,
  input  CLK,
  input  Entrada,
  input  CLR,
  output Q,
  output Q_prime
);

  wire nand_1_out;

  nand nand_1 (nand_1_out, JMP, END);
  T_Flip_Flop t_ff_1 (.clk(CLK), .T(Entrada), .Q(Q), .Qn(Q_prime), .preset(nand_1_out), .reset(CLR));
endmodule

module contador (
  input  CLK,
  input  in_2,
  output [7:0] out_3
);

  wire and_1_out, and_2_out, and_3_out, and_4_out, and_5_out, and_6_out;

  flip_flop_alterado flip_flop_alterado_1 (
    .CLK(CLK), .Entrada(1'b1), .CLR(in_2), .Q(out_3[0]));  // open: JMP, END, Q_prime
  flip_flop_alterado flip_flop_alterado_2 (
    .CLK(CLK), .Entrada(out_3[0]), .CLR(in_2), .Q(out_3[1]));  // open: JMP, END, Q_prime
  and and_1 (and_1_out, out_3[1], out_3[0]);
  flip_flop_alterado flip_flop_alterado_3 (
    .CLK(CLK), .Entrada(and_1_out), .CLR(in_2), .Q(out_3[2]));  // open: JMP, END, Q_prime
  and and_2 (and_2_out, out_3[2], and_1_out);
  Hex_Digit_Display hex_digit_display_1 (.value(out_3[7:4]));  // open: dp
  flip_flop_alterado flip_flop_alterado_4 (
    .CLK(CLK), .Entrada(and_2_out), .CLR(in_2), .Q(out_3[3]));  // open: JMP, END, Q_prime
  and and_3 (and_3_out, out_3[3], and_2_out);
  Hex_Digit_Display hex_digit_display_2 (.value(out_3[3:0]));  // open: dp
  flip_flop_alterado flip_flop_alterado_5 (
    .CLK(CLK), .Entrada(and_3_out), .CLR(in_2), .Q(out_3[4]));  // open: JMP, END, Q_prime
  and and_4 (and_4_out, out_3[4], and_3_out);
  flip_flop_alterado flip_flop_alterado_6 (
    .CLK(CLK), .Entrada(and_4_out), .CLR(in_2), .Q(out_3[5]));  // open: JMP, END, Q_prime
  and and_5 (and_5_out, out_3[5], and_4_out);
  flip_flop_alterado flip_flop_alterado_7 (
    .CLK(CLK), .Entrada(and_5_out), .CLR(in_2), .Q(out_3[6]));  // open: JMP, END, Q_prime
  and and_6 (and_6_out, out_3[6], and_5_out);
  flip_flop_alterado flip_flop_alterado_8 (
    .CLK(CLK), .Entrada(and_6_out), .CLR(in_2), .Q(out_3[7]));  // open: JMP, END, Q_prime
endmodule
