// Logisim project ContadorSincrono8Bits.circ as structural Verilog: 1 circuit, main circuit main
module main (
);

  wire clock_1_out, undriven;
  wire [2:2] undriven_2;

  Clock clock_1 (.out(clock_1_out));
  J_K_Flip_Flop j_k_ff_1 (.clk(clock_1_out), .K(1'b1), .reset(undriven));  // open: J, Q, Qn, preset
  J_K_Flip_Flop j_k_ff_2 (.clk(clock_1_out), .K(undriven), .reset(undriven));  // open: J, Q, Qn, preset
  J_K_Flip_Flop j_k_ff_3 (.clk(clock_1_out), .K(undriven), .reset(undriven));  // open: J, Q, Qn, preset
  J_K_Flip_Flop j_k_ff_4 (.clk(clock_1_out), .K(undriven), .reset(undriven));  // open: J, Q, Qn, preset
  _7_Segment_Display u_7_segment_display_1 (.d(undriven_2[2]));  // open: g, f, a, b, e, c, dp
endmodule
