// Logisim project DivisorBits.circ as structural Verilog
module main (
  input  [15:0] in_1,
  output [3:0] Operando,
  output [3:0] \Dinsponível ,
  output [1:0] ULA,
  output [1:0] JUMP,
  output [1:0] RgTO,
  output [1:0] RgTIn
);


  assign \Dinsponível  = in_1[7:4];
  assign JUMP = in_1[11:10];
  assign Operando = in_1[3:0];
  assign RgTIn = in_1[13:12];
  assign RgTO = in_1[15:14];
  assign ULA = in_1[9:8];
endmodule
